// Logisim project cpu.circ as structural Verilog: 14 circuits, main circuit main
module main (
);

  wire ALC, ALO, ALS, and_1_out, clock_1_out, FE, HLT, IE, IRE, IRO, JMP, MAE, not_1_out, PCE, PCO, RAE, RAO,
       XE, XO, YE, YO, ZE, ZO;
  wire [2:0] alu_1_cf, XReg_regouta_2, YReg_regouta_2;
  wire [4:0] InstructionRegister_regouta_2;
  wire [10:0] InstructionRegister_regouta;
  wire [12:0] XReg_regouta, YReg_regouta;
  wire [15:0] alu_1_aluout, FlagsReg_regouta, MemoryAddressRegister_regouta, programcounter_1_counterout,
       ZReg_regouta;
  wire [15:11] InstructionRegister_regout;

  ControlLogic controllogic_1 (
    .CLK(and_1_out), .InstructionOpcode(InstructionRegister_regouta_2), .Flags(FlagsReg_regouta[7:0]),
    .ControlBits({HLT, PCE, PCO, JMP, XE, XO, YE, YO, ZE, ZO, IRE, IRO, MAE, RAE, RAO, FE, ALO, ALS, ALC, IE}));
  Clock clock_1 (.out(clock_1_out));
  not not_1 (not_1_out, HLT);
  ALU alu_1 (
    .XReg({XReg_regouta_2, XReg_regouta}), .YReg({YReg_regouta_2, YReg_regouta}), .ALS(ALS), .ALC(ALC),
    .ALUOut(alu_1_aluout), .CF(alu_1_cf[0]), .ZF(alu_1_cf[1]), .PF(alu_1_cf[2]));
  and and_1 (and_1_out, clock_1_out, not_1_out);
  LED led_1 (.in(programcounter_1_counterout[15]));
  ProgramCounter programcounter_1 (
    .JMP(JMP), .PCE(PCE), .PCO(PCO), .CLK(and_1_out), .CounterIn(programcounter_1_counterout[10:0]),
    .CounterOut(programcounter_1_counterout[10:0]));
  LED led_2 (.in(programcounter_1_counterout[14]));
  LED led_3 (.in(programcounter_1_counterout[13]));
  LED led_4 (.in(programcounter_1_counterout[12]));
  LED led_5 (.in(programcounter_1_counterout[11]));
  assign programcounter_1_counterout = ALO ? alu_1_aluout : 16'bz;  // Controlled_Buffer controlled_buffer_1
  Pull_Resistor pull_resistor_1 (.node(programcounter_1_counterout[15]));
  Pull_Resistor pull_resistor_2 (.node(programcounter_1_counterout[14]));
  Pull_Resistor pull_resistor_3 (.node(programcounter_1_counterout[13]));
  Pull_Resistor pull_resistor_4 (.node(programcounter_1_counterout[12]));
  LED led_6 (.in(programcounter_1_counterout[10]));
  LED led_7 (.in(programcounter_1_counterout[9]));
  LED led_8 (.in(programcounter_1_counterout[8]));
  Pull_Resistor pull_resistor_5 (.node(programcounter_1_counterout[11]));
  Pull_Resistor pull_resistor_6 (.node(programcounter_1_counterout[10]));
  LED led_9 (.in(programcounter_1_counterout[7]));
  LED led_10 (.in(programcounter_1_counterout[6]));
  LED led_11 (.in(programcounter_1_counterout[5]));
  LED led_12 (.in(programcounter_1_counterout[4]));
  Pull_Resistor pull_resistor_7 (.node(programcounter_1_counterout[9]));
  Pull_Resistor pull_resistor_8 (.node(programcounter_1_counterout[8]));
  Pull_Resistor pull_resistor_9 (.node(programcounter_1_counterout[7]));
  Pull_Resistor pull_resistor_10 (.node(programcounter_1_counterout[6]));
  Pull_Resistor pull_resistor_11 (.node(programcounter_1_counterout[5]));
  Pull_Resistor pull_resistor_12 (.node(programcounter_1_counterout[4]));
  Pull_Resistor pull_resistor_13 (.node(programcounter_1_counterout[3]));
  Pull_Resistor pull_resistor_14 (.node(programcounter_1_counterout[2]));
  LED led_13 (.in(programcounter_1_counterout[3]));
  LED led_14 (.in(programcounter_1_counterout[2]));
  LED led_15 (.in(programcounter_1_counterout[1]));
  LED led_16 (.in(programcounter_1_counterout[0]));
  Pull_Resistor pull_resistor_15 (.node(programcounter_1_counterout[1]));
  Pull_Resistor pull_resistor_16 (.node(programcounter_1_counterout[0]));
  CPUReg FlagsReg (
    .RegIn({{13{1'b0}}, alu_1_cf}), .CE(FE), .CO(1'b1), .CLK(and_1_out), .RegOutA(FlagsReg_regouta));  // open: RegOut
  CPUReg XReg (
    .RegIn(programcounter_1_counterout), .CE(XE), .CO(XO), .CLK(and_1_out),
    .RegOut(programcounter_1_counterout), .RegOutA({XReg_regouta_2, XReg_regouta}));
  CPUReg YReg (
    .RegIn(programcounter_1_counterout), .CE(YE), .CO(YO), .CLK(and_1_out),
    .RegOut(programcounter_1_counterout), .RegOutA({YReg_regouta_2, YReg_regouta}));
  CPUReg ZReg (
    .RegIn(programcounter_1_counterout), .CE(ZE), .CO(ZO), .CLK(and_1_out),
    .RegOut(programcounter_1_counterout), .RegOutA(ZReg_regouta));
  CPUReg InstructionRegister (
    .RegIn(programcounter_1_counterout), .CE(IRE), .CO(IRO), .CLK(and_1_out),
    .RegOut({InstructionRegister_regout, programcounter_1_counterout[10:0]}),
    .RegOutA({InstructionRegister_regouta_2, InstructionRegister_regouta}));
  CPUReg MemoryAddressRegister (
    .RegIn({{5{1'b0}}, programcounter_1_counterout[10:0]}), .CE(MAE), .CO(1'b1), .CLK(and_1_out),
    .RegOutA(MemoryAddressRegister_regouta));  // open: RegOut
  CPURam cpuram_1 (
    .Address(MemoryAddressRegister_regouta[10:0]), .CE(RAE), .CLK(and_1_out),
    .ValueIn(programcounter_1_counterout), .CO(RAO), .ValueOut(programcounter_1_counterout));
  _7_Segment_Display u_7_segment_display_1 ();  // open: g, f, a, b, e, d, c, dp
  _7_Segment_Display u_7_segment_display_2 ();  // open: g, f, a, b, e, d, c, dp
  // BCD_to_7_Segment_decoder bcd_to_7_segment_decoder_1: pin names not known
  // BCD_to_7_Segment_decoder bcd_to_7_segment_decoder_2: pin names not known
  // Binary_to_BCD_converter #(.binvalue(13)) binary_to_bcd_converter_1: pin names not known; wires that end beside it: programcounter_1_counterout, XReg_regouta
  _7_Segment_Display u_7_segment_display_3 ();  // open: g, f, a, b, e, d, c, dp
  _7_Segment_Display u_7_segment_display_4 ();  // open: g, f, a, b, e, d, c, dp
  // BCD_to_7_Segment_decoder bcd_to_7_segment_decoder_3: pin names not known
  // BCD_to_7_Segment_decoder bcd_to_7_segment_decoder_4: pin names not known
  // Binary_to_BCD_converter #(.binvalue(13)) binary_to_bcd_converter_2: pin names not known; wires that end beside it: YReg_regouta
  _7_Segment_Display u_7_segment_display_5 ();  // open: g, f, a, b, e, d, c, dp
  // BCD_to_7_Segment_decoder bcd_to_7_segment_decoder_5: pin names not known; wires that end beside it: ZReg_regouta
  // Binary_to_BCD_converter #(.binvalue(5)) binary_to_bcd_converter_3: pin names not known; wires that end beside it: InstructionRegister_regouta_2
  _7_Segment_Display u_7_segment_display_6 ();  // open: g, f, a, b, e, d, c, dp
  // BCD_to_7_Segment_decoder bcd_to_7_segment_decoder_6: pin names not known
  _7_Segment_Display u_7_segment_display_7 ();  // open: g, f, a, b, e, d, c, dp
  // BCD_to_7_Segment_decoder bcd_to_7_segment_decoder_7: pin names not known
  _7_Segment_Display u_7_segment_display_8 ();  // open: g, f, a, b, e, d, c, dp
  // BCD_to_7_Segment_decoder bcd_to_7_segment_decoder_8: pin names not known
  _7_Segment_Display u_7_segment_display_9 ();  // open: g, f, a, b, e, d, c, dp
  // BCD_to_7_Segment_decoder bcd_to_7_segment_decoder_9: pin names not known
  _7_Segment_Display u_7_segment_display_10 ();  // open: g, f, a, b, e, d, c, dp
  // BCD_to_7_Segment_decoder bcd_to_7_segment_decoder_10: pin names not known
  _7_Segment_Display u_7_segment_display_11 ();  // open: g, f, a, b, e, d, c, dp
  // BCD_to_7_Segment_decoder bcd_to_7_segment_decoder_11: pin names not known
  // Binary_to_BCD_converter #(.binvalue(11)) binary_to_bcd_converter_4: pin names not known; wires that end beside it: InstructionRegister_regouta
  _7_Segment_Display u_7_segment_display_12 ();  // open: g, f, a, b, e, d, c, dp
  _7_Segment_Display u_7_segment_display_13 ();  // open: g, f, a, b, e, d, c, dp
  // BCD_to_7_Segment_decoder bcd_to_7_segment_decoder_12: pin names not known
  // BCD_to_7_Segment_decoder bcd_to_7_segment_decoder_13: pin names not known
  _7_Segment_Display u_7_segment_display_14 ();  // open: g, f, a, b, e, d, c, dp
  // BCD_to_7_Segment_decoder bcd_to_7_segment_decoder_14: pin names not known

  // Notes on the sheet:
  //   Control Bits
  //   Clock
  //   Opcode
  //   Operand
endmodule

module ALU (
  input  [15:0] XReg,
  input  [15:0] YReg,
  input  ALS,
  input  ALC,
  output [15:0] ALUOut,
  output CF,
  output ZF,
  output PF
);

  wire not_1_out;
  wire [15:0] controlled_buffer_1_out, xorregister_1_outreg;

  assign controlled_buffer_1_out = ALC ? 16'h1 : 16'bz;  // Controlled_Buffer controlled_buffer_1
  not not_1 (not_1_out, ALC);
  assign controlled_buffer_1_out = not_1_out ? YReg : 16'bz;  // Controlled_Buffer controlled_buffer_2
  FullAdder16Bit fulladder16bit_1 (.CI(ALS), .A(XReg), .B(xorregister_1_outreg), .S(ALUOut), .CO(CF));
  XORRegister xorregister_1 (.InReg(controlled_buffer_1_out), .CE(ALS), .OutReg(xorregister_1_outreg));
  ZeroRegister zeroregister_1 (.RegIn(ALUOut), .ZeroReg(ZF));
  not not_2 (PF, ALUOut[0]);
  // Binary_to_BCD_converter #(.binvalue(11)) binary_to_bcd_converter_1: pin names not known
endmodule

module HalfAdder (
  input  A,
  input  B,
  output CO,
  output S
);

  and and_1 (CO, A, B);
  xor xor_1 (S, A, B);
endmodule

module FullAdder (
  input  CI,
  input  A,
  input  B,
  output S,
  output CO
);

  wire halfadder_1_co, halfadder_2_co, halfadder_2_s;

  HalfAdder halfadder_1 (.A(CI), .B(halfadder_2_s), .CO(halfadder_1_co), .S(S));
  HalfAdder halfadder_2 (.A(A), .B(B), .CO(halfadder_2_co), .S(halfadder_2_s));
  or or_1 (CO, halfadder_1_co, halfadder_2_co);
endmodule

module FullAdder4Bit (
  input  CI,
  input  [3:0] A,
  input  [3:0] B,
  output [3:0] S,
  output CO
);

  wire fulladder_1_co, fulladder_2_co, fulladder_3_co;

  FullAdder fulladder_1 (.CI(CI), .A(A[0]), .B(B[0]), .S(S[0]), .CO(fulladder_1_co));
  FullAdder fulladder_2 (.CI(fulladder_1_co), .A(A[1]), .B(B[1]), .S(S[1]), .CO(fulladder_2_co));
  FullAdder fulladder_3 (.CI(fulladder_2_co), .A(A[2]), .B(B[2]), .S(S[2]), .CO(fulladder_3_co));
  FullAdder fulladder_4 (.CI(fulladder_3_co), .A(A[3]), .B(B[3]), .S(S[3]), .CO(CO));
endmodule

module FullAdder8Bit (
  input  CI,
  input  [7:0] A,
  input  [7:0] B,
  output [7:0] S,
  output CO
);

  wire fulladder4bit_1_co;

  FullAdder4Bit fulladder4bit_1 (.CI(CI), .A(A[3:0]), .B(B[3:0]), .S(S[3:0]), .CO(fulladder4bit_1_co));
  FullAdder4Bit fulladder4bit_2 (.CI(fulladder4bit_1_co), .A(A[7:4]), .B(B[7:4]), .S(S[7:4]), .CO(CO));
endmodule

module FullAdder16Bit (
  input  CI,
  input  [15:0] A,
  input  [15:0] B,
  output [15:0] S,
  output CO
);

  wire fulladder8bit_1_co;

  FullAdder8Bit fulladder8bit_1 (.CI(CI), .A(A[7:0]), .B(B[7:0]), .S(S[7:0]), .CO(fulladder8bit_1_co));
  FullAdder8Bit fulladder8bit_2 (.CI(fulladder8bit_1_co), .A(A[15:8]), .B(B[15:8]), .S(S[15:8]), .CO(CO));
endmodule

module XORRegister (
  input  [15:0] InReg,
  input  CE,
  output [15:0] OutReg
);

  xor xor_1 (OutReg[0], InReg[0], CE);
  xor xor_2 (OutReg[1], InReg[1], CE);
  xor xor_3 (OutReg[2], InReg[2], CE);
  xor xor_4 (OutReg[3], InReg[3], CE);
  xor xor_5 (OutReg[4], InReg[4], CE);
  xor xor_6 (OutReg[5], InReg[5], CE);
  xor xor_7 (OutReg[6], InReg[6], CE);
  xor xor_8 (OutReg[7], InReg[7], CE);
  xor xor_9 (OutReg[8], InReg[8], CE);
  xor xor_10 (OutReg[9], InReg[9], CE);
  xor xor_11 (OutReg[10], InReg[10], CE);
  xor xor_12 (OutReg[11], InReg[11], CE);
  xor xor_13 (OutReg[12], InReg[12], CE);
  xor xor_14 (OutReg[13], InReg[13], CE);
  xor xor_15 (OutReg[14], InReg[14], CE);
  xor xor_16 (OutReg[15], InReg[15], CE);
endmodule

module MicrocodeAddress (
  input  [2:0] InstructionStep,
  input  [4:0] InstructionOpcode,
  input  [7:0] Flags,
  output [10:0] Address
);


  assign Address = {Flags[2:0], InstructionOpcode, InstructionStep};
endmodule

module ControlLogic (
  input  CLK,
  input  [4:0] InstructionOpcode,
  input  [7:0] Flags,
  output [19:0] ControlBits
);

  wire IE, not_1_out;
  wire [2:0] InstructionStepCounter_q;
  wire [10:0] microcodeaddress_1_address;

  ROM #(.addrWidth(11), .dataWidth(20)) rom_1 (.addr(microcodeaddress_1_address), .data(ControlBits));
  MicrocodeAddress microcodeaddress_1 (
    .InstructionStep(InstructionStepCounter_q), .InstructionOpcode(InstructionOpcode), .Flags(Flags),
    .Address(microcodeaddress_1_address));
  Counter #(.max('h7), .width(3)) InstructionStepCounter (
    .load(IE), .up(1'b1), .count(1'b1), .clk(not_1_out), .D(3'b000), .Q(InstructionStepCounter_q));  // open: clr, carry
  not not_1 (not_1_out, CLK);

  // Notes on the sheet:
  //   contents of rom_1 (hex, n*v repeats v):
  //   20080 40220 6*0 20080 40220 180 8021 4*0 20080 40220 180 2021 4*0 20080 40220 180 821 4*0 20080
  //   40220 8101 5*0 20080 40220 2101 5*0 20080 40220 901 5*0 20080 40220 180 2020 819 0 0 0 20080 40220
  //   180 2020 81d 0 0 0 20080 40220 10101 5*0 20080 40220 180 801b 4*0 20080 40220 180 201b 4*0 20080
  //   40220 180 81b 4*0 20080 40220 6*0 20080 40220 6*0 20080 40220 6*0 20080 40220 6*0 20080 40220 6*0
  //   20080 40220 6*0 20080 40220 6*0 20080 40220 6*0 20080 40220 6*0 20080 40220 6*0 20080 40220 6*0
  //   20080 40220 6*0 20080 40220 6*0 20080 40220 6*0 20080 40220 6*0 20080 40220 6*0 20080 40220 6*0
  //   20080 40220 6*0 20080 40220 80001 5*0 20080 40220 6*0 20080 40220 180 8021 4*0 20080 40220 180 2021
  //   4*0 20080 40220 180 821 4*0 20080 40220 8101 5*0 20080 40220 2101 5*0 20080 40220 901 5*0 20080
  //   40220 180 2020 819 0 0 0 20080 40220 180 2020 81d 0 0 0 20080 40220 10101 5*0 20080 40220 180 801b
  //   4*0 20080 40220 180 201b 4*0 20080 40220 180 81b 4*0 20080 40220 6*0 20080 40220 10101 5*0 20080
  //   40220 6*0 20080 40220 6*0 20080 40220 6*0 20080 40220 6*0 20080 40220 6*0 20080 40220 6*0 20080
  //   40220 6*0 20080 40220 6*0 20080 40220 6*0 20080 40220 6*0 20080 40220 6*0 20080 40220 6*0 20080
  //   40220 6*0 20080 40220 6*0 20080 40220 6*0 20080 40220 6*0 20080 40220 80001 5*0 20080 40220 6*0
  //   20080 40220 180 8021 4*0 20080 40220 180 2021 4*0 20080 40220 180 821 4*0 20080 40220 8101 5*0 20080
  //   40220 2101 5*0 20080 40220 901 5*0 20080 40220 180 2020 819 0 0 0 20080 40220 180 2020 81d 0 0 0
  //   20080 40220 10101 5*0 20080 40220 180 801b 4*0 20080 40220 180 201b 4*0 20080 40220 180 81b 4*0
  //   20080 40220 10101 5*0 20080 40220 6*0 20080 40220 6*0 20080 40220 6*0 20080 40220 6*0 20080 40220
  //   6*0 20080 40220 6*0 20080 40220 6*0 20080 40220 6*0 20080 40220 6*0 20080 40220 6*0 20080 40220 6*0
  //   20080 40220 6*0 20080 40220 6*0 20080 40220 6*0 20080 40220 6*0 20080 40220 6*0 20080 40220 6*0
  //   20080 40220 80001 5*0 20080 40220 6*0 20080 40220 180 8021 4*0 20080 40220 180 2021 4*0 20080 40220
  //   180 821 4*0 20080 40220 8101 5*0 20080 40220 2101 5*0 20080 40220 901 5*0 20080 40220 180 2020 819 0
  //   0 0 20080 40220 180 2020 81d 0 0 0 20080 40220 10101 5*0 20080 40220 180 801b 4*0 20080 40220 180
  //   201b 4*0 20080 40220 180 81b 4*0 20080 40220 10101 5*0 20080 40220 10101 5*0 20080 40220 6*0 20080
  //   40220 6*0 20080 40220 6*0 20080 40220 6*0 20080 40220 6*0 20080 40220 6*0 20080 40220 6*0 20080
  //   40220 6*0 20080 40220 6*0 20080 40220 6*0 20080 40220 6*0 20080 40220 6*0 20080 40220 6*0 20080
  //   40220 6*0 20080 40220 6*0 20080 40220 6*0 20080 40220 80001 5*0 20080 40220 6*0 20080 40220 180 8021
  //   4*0 20080 40220 180 2021 4*0 20080 40220 180 821 4*0 20080 40220 8101 5*0 20080 40220 2101 5*0 20080
  //   40220 901 5*0 20080 40220 180 2020 819 0 0 0 20080 40220 180 2020 81d 0 0 0 20080 40220 10101 5*0
  //   20080 40220 180 801b 4*0 20080 40220 180 201b 4*0 20080 40220 180 81b 4*0 20080 40220 6*0 20080
  //   40220 6*0 20080 40220 10101 5*0 20080 40220 6*0 20080 40220 6*0 20080 40220 6*0 20080 40220 6*0
  //   20080 40220 6*0 20080 40220 6*0 20080 40220 6*0 20080 40220 6*0 20080 40220 6*0 20080 40220 6*0
  //   20080 40220 6*0 20080 40220 6*0 20080 40220 6*0 20080 40220 6*0 20080 40220 6*0 20080 40220 80001
  //   5*0 20080 40220 6*0 20080 40220 180 8021 4*0 20080 40220 180 2021 4*0 20080 40220 180 821 4*0 20080
  //   40220 8101 5*0 20080 40220 2101 5*0 20080 40220 901 5*0 20080 40220 180 2020 819 0 0 0 20080 40220
  //   180 2020 81d 0 0 0 20080 40220 10101 5*0 20080 40220 180 801b 4*0 20080 40220 180 201b 4*0 20080
  //   40220 180 81b 4*0 20080 40220 6*0 20080 40220 10101 5*0 20080 40220 10101 5*0 20080 40220 6*0 20080
  //   40220 6*0 20080 40220 6*0 20080 40220 6*0 20080 40220 6*0 20080 40220 6*0 20080 40220 6*0 20080
  //   40220 6*0 20080 40220 6*0 20080 40220 6*0 20080 40220 6*0 20080 40220 6*0 20080 40220 6*0 20080
  //   40220 6*0 20080 40220 6*0 20080 40220 80001 5*0 20080 40220 6*0 20080 40220 180 8021 4*0 20080 40220
  //   180 2021 4*0 20080 40220 180 821 4*0 20080 40220 8101 5*0 20080 40220 2101 5*0 20080 40220 901 5*0
  //   20080 40220 180 2020 819 0 0 0 20080 40220 180 2020 81d 0 0 0 20080 40220 10101 5*0 20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
endmodule

module ProgramCounter (
  input  JMP,
  input  PCE,
  input  PCO,
  input  CLK,
  input  [10:0] CounterIn,
  output [10:0] CounterOut
);

  wire [10:0] controlled_buffer_1_out, ProgramCounter_q;

  assign controlled_buffer_1_out = JMP ? CounterIn : 11'bz;  // Controlled_Buffer controlled_buffer_1
  Counter #(.max('h7ff), .width(11)) ProgramCounter (
    .load(JMP), .up(1'b1), .count(PCE), .clk(CLK), .D(controlled_buffer_1_out), .Q(ProgramCounter_q));  // open: clr, carry
  assign CounterOut = PCO ? ProgramCounter_q : 11'bz;  // Controlled_Buffer controlled_buffer_2
endmodule

module CPUReg (
  input  [15:0] RegIn,
  input  CE,
  input  CO,
  input  CLK,
  output [15:0] RegOut,
  output [15:0] RegOutA
);

  wire [15:0] controlled_buffer_1_out;

  assign controlled_buffer_1_out = CE ? RegIn : 16'bz;  // Controlled_Buffer controlled_buffer_1
  Register #(.width(16)) register_1 (.D(controlled_buffer_1_out), .en(CE), .clk(CLK), .Q(RegOutA));  // open: clr
  assign RegOut = CO ? RegOutA : 16'bz;  // Controlled_Buffer controlled_buffer_2
endmodule

module CPURam (
  input  [10:0] Address,
  input  CE,
  input  CLK,
  input  [15:0] ValueIn,
  input  CO,
  output [15:0] ValueOut
);

  wire [15:0] controlled_buffer_1_out, ram_1_dout;

  RAM #(.addrWidth(11), .dataWidth(16), .enables("line"), .\type ("nonvolatile")) ram_1 (
    .addr(Address), .we(CE), .clk(CLK), .din(controlled_buffer_1_out), .dout(ram_1_dout));
  assign controlled_buffer_1_out = CE ? ValueIn : 16'bz;  // Controlled_Buffer controlled_buffer_1
  assign ValueOut = CO ? ram_1_dout : 16'bz;  // Controlled_Buffer controlled_buffer_2
endmodule

module ZeroRegister (
  input  [15:0] RegIn,
  output ZeroReg
);

  wire and_1_out, and_2_out, and_3_out, and_4_out, and_5_out, and_6_out, nor_1_out, nor_2_out, nor_3_out,
       nor_4_out, nor_5_out, nor_6_out, nor_7_out, nor_8_out;

  nor nor_1 (nor_1_out, RegIn[15], RegIn[14]);
  nor nor_2 (nor_2_out, RegIn[13], RegIn[12]);
  nor nor_3 (nor_3_out, RegIn[11], RegIn[10]);
  nor nor_4 (nor_4_out, RegIn[9], RegIn[8]);
  nor nor_5 (nor_5_out, RegIn[7], RegIn[6]);
  nor nor_6 (nor_6_out, RegIn[5], RegIn[4]);
  nor nor_7 (nor_7_out, RegIn[3], RegIn[2]);
  nor nor_8 (nor_8_out, RegIn[1], RegIn[0]);
  and and_1 (and_1_out, nor_1_out, nor_2_out);
  and and_2 (and_2_out, nor_3_out, nor_4_out);
  and and_3 (and_3_out, nor_5_out, nor_6_out);
  and and_4 (and_4_out, nor_7_out, nor_8_out);
  and and_5 (and_5_out, and_1_out, and_2_out);
  and and_6 (and_6_out, and_3_out, and_4_out);
  and and_7 (ZeroReg, and_5_out, and_6_out);
endmodule
